# Fritzing sketch speech-controlled-robot-schematic (saved by Fritzing 0.9.3b)

parts:
  S1 = H-Bridge with L298N
  M1 = DC Motor
  M2 = DC Motor
  Part1 = Arduino Nano (Rev3.0)
  Part2 = Bluetooth HC-05 Macho
  BAT1 = BC9VPC [package=bc9vpc]

nets:
  12V: S1.12V, Part1.VIN, BAT1.V+
  N1: S1.GND, BAT1.V-
  N2: S1.IN1, Part1.D5
  N3: S1.IN2, Part1.D4
  N4: S1.IN3, Part1.D3
  N5: S1.IN4, Part1.D2
  N6: S1.M1-01, M2.pin_2
  N7: S1.M1-02, M2.pin_1
  N8: S1.M2-01, M1.pin_2
  N9: S1.M2-02, M1.pin_1
  N10: Part1.D1/TX, Part2.RXD
  N11: Part1.D0/RX, Part2.TXD
  GND: Part1.GND, Part2.GND
  5V: Part1.5V, Part2.VCC

custom parts:
  H-Bridge with L298N: h-bridge
  DC Motor: Your standard DC Motor
